# Fritzing sketch Design (saved by Fritzing 0.9.4)
breadboards: 1

parts:
  M1 = Arduino Uno WIFI REV2
  M2 = DC Motor
  M5 = DC Motor
  L298N1 = L298N DC motor driver
  L298N2 = L298N DC motor driver
  M6 = DC Motor
  M7 = DC Motor
  Stromversorgung_Beradboard1 = Stromversorgung Beradboard [package=THT]
  Espessif_Serial_Wifi_Modul_1 = ESP8266 ESP01 [part_number=ESP8266 package=THT]  # not connected
  VCC1 = Battery

nets:
  N1: M1.5V, Stromversorgung_Beradboard1.Ground_1#14
  GND: M1.GND, M1.ISCP_GND, L298N1.GND, L298N2.GND, Stromversorgung_Beradboard1.+5_/_+3_Volt_4, VCC1.-
  N2: M1.D2, L298N2.IN4
  N3: M1.D3_PWM, L298N2.IN3
  N4: M1.D4, L298N2.IN2
  N5: M1.D5_PWM, L298N2.IN1
  N6: M1.D6_PWM, L298N1.IN4
  N7: M1.D7, L298N1.IN3
  N8: M1.D8, L298N1.IN2
  N9: M1.D9_PWM, L298N1.IN1
  N10: M1.D10_PWM/SS, L298N1.ENA, L298N1.ENB, L298N2.ENA, L298N2.ENB
  N11: M2.pin_1, L298N1.OUT2
  N12: M2.pin_2, L298N1.OUT1
  N13: M5.pin_1, L298N1.OUT4
  N14: M5.pin_2, L298N1.OUT3
  12V: L298N1.12V, L298N2.12V, Stromversorgung_Beradboard1.Ground_1#15, VCC1.+
  N15: L298N2.OUT1, M6.pin_2
  N16: L298N2.OUT2, M6.pin_1
  N17: L298N2.OUT3, M7.pin_2
  N18: L298N2.OUT4, M7.pin_1

custom parts:
  Arduino Uno WIFI REV2: The Arduino Uno WIFI REV2 is a microcontroller board based on the ATmega 4809. It has 14 digital input/output pins (of which 5 can be used as PWM outputs), 6 analog inputs, a 16 MHz ceramic resonator, a USB connection, a power jack, an ICSP header, and a reset button. It also has a WIFI controller with a secure ECC608 crypto unit and an internal IMU. It contains everything needed to support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
  L298N DC motor driver: 2x DC motor driver with 78M05 positive voltage regulator (7..35 V) L298N: max 46 V, 2 A Set 5 V Enable jumper to enable 5 V regultor (needed for the L298N) and +5 V output at screw terminal or supply external +5 V at screw terminal Set ENA and/or ENB to +5 V to enable motor permanently or supply ENA and/or ENB with PWM signal IN1 and IN2 set rotation directory for motor A (OUT1/OUT2) IN2 and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
  ESP8266 ESP01: Generic WiFi Module based on the ESP8266 with onboard PCB antenna and UART communications
