# Fritzing sketch ArduinoMotorn (saved by Fritzing 0.9.4)
breadboards: 1

parts:
  M2 = DC Motor
  M5 = DC Motor
  L298N1 = L298N DC motor driver
  L298N2 = L298N DC motor driver
  M6 = DC Motor
  M7 = DC Motor
  Stromversorgung_Beradboard1 = Stromversorgung Beradboard [package=THT]
  Espessif_Serial_Wifi_Modul_1 = ESP8266 ESP01 [part_number=ESP8266 package=THT]
  VCC1 = Battery
  Part1 = Arduino Uno (Rev3)

nets:
  N1: M2.pin_1, L298N1.OUT2
  N2: M2.pin_2, L298N1.OUT1
  N3: M5.pin_1, L298N1.OUT4
  N4: M5.pin_2, L298N1.OUT3
  12V: L298N1.12V, L298N2.12V, Stromversorgung_Beradboard1.Ground_1#15
  GND: L298N1.GND, L298N2.GND, Stromversorgung_Beradboard1.+5_/_+3_Volt_4#13, Espessif_Serial_Wifi_Modul_1.GND, VCC1.-, Part1.GND
  N5: L298N1.ENA, L298N1.ENB, L298N2.ENA, L298N2.ENB, Part1.D10_PWM/SS
  N6: L298N1.IN1, Part1.D9_PWM
  N7: L298N1.IN2, Part1.D8
  N8: L298N1.IN3, Part1.D7
  N9: L298N1.IN4, Part1.D6_PWM
  N10: L298N2.OUT1, M6.pin_2
  N11: L298N2.OUT2, M6.pin_1
  N12: L298N2.OUT3, M7.pin_2
  N13: L298N2.OUT4, M7.pin_1
  N14: L298N2.IN1, Part1.D2
  N15: L298N2.IN2, Part1.D3_PWM
  N16: L298N2.IN3, Part1.D4
  N17: L298N2.IN4, Part1.D5_PWM
  N18: Espessif_Serial_Wifi_Modul_1.RXD, Part1.D0/RX
  N19: Espessif_Serial_Wifi_Modul_1.TXD, Part1.D1/TX
  N20: Espessif_Serial_Wifi_Modul_1.VCC, Espessif_Serial_Wifi_Modul_1.CH_PD

custom parts:
  L298N DC motor driver: 2x DC motor driver with 78M05 positive voltage regulator (7..35 V) L298N: max 46 V, 2 A Set 5 V Enable jumper to enable 5 V regultor (needed for the L298N) and +5 V output at screw terminal or supply external +5 V at screw terminal Set ENA and/or ENB to +5 V to enable motor permanently or supply ENA and/or ENB with PWM signal IN1 and IN2 set rotation directory for motor A (OUT1/OUT2) IN2 and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
  ESP8266 ESP01: Generic WiFi Module based on the ESP8266 with onboard PCB antenna and UART communications
