# Fritzing sketch ESP8266 Arduino (saved by Fritzing 0.9.4)
breadboards: 1

parts:
  Espessif_Serial_Wifi_Modul_1 = ESP8266 ESP01 [part_number=ESP8266 package=THT]
  Part1 = Arduino Uno (Rev3)

nets:
  GND: Espessif_Serial_Wifi_Modul_1.GND, Part1.GND
  N1: Espessif_Serial_Wifi_Modul_1.RXD, Part1.D0/RX
  N2: Espessif_Serial_Wifi_Modul_1.TXD, Part1.D1/TX
  VCC: Espessif_Serial_Wifi_Modul_1.VCC, Espessif_Serial_Wifi_Modul_1.CH_PD, Part1.3V3

custom parts:
  ESP8266 ESP01: Generic WiFi Module based on the ESP8266 with onboard PCB antenna and UART communications
